// Logisim project 150120018_150121534_150120060_150121071.circ as structural Verilog: 24 circuits, main circuit andGate
module main (
  input  clear,
  output [17:0] out_2,
  output [17:0] out_3,
  output [17:0] out_4,
  output [17:0] out_5
);

  wire and_1_out, and_2_out, CF, clock, fetchEnable, isALU, isCMP, isCmpJump, isJMP, JumpForCmp,
       loadRegister, MemoryRead, MemoryWrite, or_1_out, or_2_out, pcEnable, Register_Write_Enable, ZF;
  wire [1:0] NORCODE__NANDCODE__ANDCODE__ADDCODE;
  wire [2:0] CmpJumpCode, multiplexer_1_out;
  wire [3:0] counter_1_output_2, JUMPCODE__OP1__source1_ST__destination, multiplexer_3_out,
       multiplexer_4_out, multiplexer_5_out, OP1, OP2__SRC2, OPCODE, Source1, Source2;
  wire [5:0] IMMEDIATE;
  wire [9:0] ADDRESS, counter_1_output;
  wire [17:0] Data_Memory_Out, IMM_18, multiplexer_2_out, R0, R1, R2, R3, R4, R5, R6, R7, R8, R9, R10, R11,
       R12, R13, R14, R15;

  or or_1 (or_1_out, and_1_out, isJMP);
  and and_1 (and_1_out, JumpForCmp, isCmpJump);
  Hex_Digit_Display hex_digit_display_1 (.value(counter_1_output[3:0]));  // open: dp
  Hex_Digit_Display hex_digit_display_2 (.value(counter_1_output_2));  // open: dp
  counter counter_1 (
    .jumpValue(ADDRESS), .isJump(or_1_out), .clock(pcEnable), .clear(clear),
    .\output ({counter_1_output[9:8], counter_1_output_2, counter_1_output[3:0]}));
  Clock clock_1 (.out(clock));
  Multiplexer #(.select(3), .width(3), .enable("false")) multiplexer_1 (
    .in0(3'b001), .in1(3'b010), .in2(3'b100), .in4(3'b000), .out(multiplexer_1_out),
    .sel({pcEnable, loadRegister, fetchEnable}));  // open: in3, in5, in6, in7
  dFlipFlop dflipflop_1 (.i(multiplexer_1_out[0]), .c(clock), .o(fetchEnable));
  dFlipFlop dflipflop_2 (.i(multiplexer_1_out[1]), .c(clock), .o(loadRegister));
  dFlipFlop dflipflop_3 (.i(multiplexer_1_out[2]), .c(clock), .o(pcEnable));
  cmpJump cmpjump_1 (.enable(isCmpJump), .Cmp_Jump_Code(CmpJumpCode), .CF(CF), .ZF(ZF), .out_5(JumpForCmp));
  ROM #(.addrWidth(10), .dataWidth(18)) rom_1 (
    .addr({counter_1_output[9:8], counter_1_output_2, counter_1_output[3:0]}), .data(out_2), .sel(1'b1));
  ALU alu_1 (.immediate(IMMEDIATE), .i1(out_3), .i2(out_4), .\output (out_5), .enable(isALU), .opcode(OPCODE));
  or or_2 (or_2_out, fetchEnable, loadRegister);
  Multiplexer #(.width(18), .disabled(0), .enable("false")) multiplexer_2 (
    .in0(out_5), .in1(Data_Memory_Out), .out(multiplexer_2_out), .sel(MemoryRead));
  Multiplexer #(.width(4), .disabled(0), .enable("false")) multiplexer_3 (
    .in0(Source1), .in1(JUMPCODE__OP1__source1_ST__destination), .out(multiplexer_3_out), .sel(MemoryWrite));
  Multiplexer #(.width(4), .disabled(0), .enable("false")) multiplexer_4 (
    .in0(multiplexer_3_out), .in1(OP1), .out(multiplexer_4_out), .sel(isCMP));
  Multiplexer #(.width(4), .disabled(0), .enable("false")) multiplexer_5 (
    .in0(Source2), .in1(OP2__SRC2), .out(multiplexer_5_out), .sel(isCMP));
  and and_2 (and_2_out, Register_Write_Enable, loadRegister);
  subtractGate CMP (.i1(out_3), .i2(out_4), .carry_flag(CF), .zero_flag(ZF), .clock(clock), .isCmp(isCMP));
  registerFile registerfile_1 (
    .Read_Register_1(multiplexer_4_out), .Read_Register_2(multiplexer_5_out),
    .data_for_write(multiplexer_2_out), .Write_Register(JUMPCODE__OP1__source1_ST__destination), .R0(R0),
    .R1(R1), .R2(R2), .R3(R3), .Register_Output_1(out_3), .R4(R4), .Register_Output_2(out_4), .R5(R5),
    .R6(R6), .R7(R7), .R8(R8), .R9(R9), .R10(R10), .R11(R11), .R12(R12), .R13(R13), .R14(R14), .R15(R15),
    .Write_Enable(and_2_out), .Clock(clock));
  Control_Unit control_unit_1 (
    .NORCODE__NANDCODE_ANDCODE__ADDCODE(NORCODE__NANDCODE__ANDCODE__ADDCODE), .OP2__SRC2(OP2__SRC2),
    .in_1(out_2), .IMM__18(IMM_18), .isCMP(isCMP), .MemoryRead(MemoryRead), .MemoryWrite(MemoryWrite),
    .OPCODE(OPCODE), .isALU(isALU), .isJMP(isJMP), .OP1(OP1), .ADDRESS(ADDRESS), .IMMEDIATE(IMMEDIATE),
    .Source_1(Source1), .Source_2(Source2), .Register_Write_Enable(Register_Write_Enable),
    .JUMPCODE__OP1__source1_ST__destination(JUMPCODE__OP1__source1_ST__destination), .isCmpJump(isCmpJump),
    .Cmp_Jump_Code(CmpJumpCode));
  RAM #(.addrWidth(10), .dataWidth(18), .bus("separate")) ram_1 (
    .addr(ADDRESS), .din(out_3), .data(Data_Memory_Out), .str(MemoryWrite), .sel(1'b1), .clk(clock),
    .ld(MemoryRead), .clr(1'b0));

  // Other names for the same wires on the sheet: Read_Source_Register_1[17:0] = out_3;
  //   Read_Source_Register_2[17:0] = out_4; Write_Register_Data[17:0] = out_5

  // Notes on the sheet:
  //   Instruction Memory
  //   ALU
  //   contents of rom_1 (hex, n*v repeats v):
  //   1001a 1045a 20001 10897 10cfb 20803 30004 50c0 1d46 1a001 1a404 1a80f 1ac07 1c003 1c806 1e011 1c807
  //   1b009 1b412 1b800 1bc0b 10884 243ed
  //   We used it for destination
  //   enable eklesek
  //   RAM
endmodule

module andGate (
  input  [17:0] i1,
  input  [17:0] i2,
  input  _16_bit,
  input  [5:0] Immediate_value,
  output [17:0] out_5
);

  wire [17:0] extendimmediatevalue_1_out_2, multiplexer_1_out;

  extendImmediateValue extendimmediatevalue_1 (.in_1(Immediate_value), .out_2(extendimmediatevalue_1_out_2));
  Multiplexer #(.width(18)) multiplexer_1 (
    .in0(i2), .in1(extendimmediatevalue_1_out_2), .out(multiplexer_1_out), .sel(_16_bit), .en(1'b1));
  assign out_5 = i1 & multiplexer_1_out;  // AND_Gate and_1, 18 bits wide
endmodule

module nandGate (
  input  [17:0] in_1,
  input  [17:0] in_2,
  output [17:0] out_3
);

  assign out_3 = ~(in_1 & in_2);  // NAND_Gate nand_1, 18 bits wide
endmodule

module norGate (
  input  [17:0] in_1,
  input  [17:0] in_2,
  output [17:0] out_3
);

  assign out_3 = ~(in_1 | in_2);  // NOR_Gate nor_1, 18 bits wide
endmodule

module halfAdder (
  input  i2,
  input  i1,
  output CarryOut,
  output s
);

  and and_1 (CarryOut, i2, i1);
  xor xor_1 (s, i2, i1);
endmodule

module fullAdder (
  input  CarryIn,
  input  i1,
  input  i2,
  output S,
  output CarryOut
);

  wire and_1_out, and_2_out, xor_2_out;

  and and_1 (and_1_out, CarryIn, xor_2_out);
  and and_2 (and_2_out, i1, i2);
  or or_1 (CarryOut, and_1_out, and_2_out);
  xor xor_1 (S, CarryIn, xor_2_out);
  xor xor_2 (xor_2_out, i1, i2);
endmodule

module dLatch (
  input  D,
  input  c,
  output Q
);

  wire and_1_out, and_2_out, halfadder_1_carryout, halfadder_1_s, multiplexer_1_out, nand_1_out, nor_1_out,
       not_1_out, register_1_q;

  halfAdder halfadder_1 (.i2(register_1_q), .i1(c), .CarryOut(halfadder_1_carryout), .s(halfadder_1_s));
  not not_1 (not_1_out, D);
  and and_1 (and_1_out, D, c);
  and and_2 (and_2_out, c, not_1_out);
  Register #(.width(1)) register_1 (.D(nand_1_out), .en(1'b1), .Q(register_1_q), .clk(c));  // open: clr
  nand nand_1 (nand_1_out, halfadder_1_s, halfadder_1_carryout);
  nor nor_1 (nor_1_out, and_1_out, Q);
  nor nor_2 (Q, multiplexer_1_out, and_2_out);
  Multiplexer #(.enable("false")) multiplexer_1 (
    .in0(1'b1), .in1(nor_1_out), .out(multiplexer_1_out), .sel(register_1_q));

  // Notes on the sheet:
  //   half adder
  //   register
endmodule

module dFlipFlop (
  input  i,
  input  c,
  output o
);

  wire dlatch_1_q, not_1_out;

  not not_1 (not_1_out, c);
  dLatch dlatch_1 (.D(i), .c(not_1_out), .Q(dlatch_1_q));
  dLatch dlatch_2 (.D(dlatch_1_q), .c(c), .Q(o));

  // Notes on the sheet:
  //   custom d latch
  //   custom d latch
endmodule

module register (
  input  [17:0] \input ,
  input  clock,
  input  enable,
  input  clear,
  output [17:0] \output 
);

  wire _0A, _1A, _2A, _3A, _4A, _5A, _6A, _7A, _8A, _9A, _10A, _11A, _12A, _13A, _14A, _15A, _16A, _17A;
  wire [0:0] not_1_out;

  dFlipFlop dflipflop_1 (.i(_17A), .c(clock), .o(\output [17]));
  dFlipFlop dflipflop_2 (.i(_15A), .c(clock), .o(\output [15]));
  dFlipFlop dflipflop_3 (.i(_16A), .c(clock), .o(\output [16]));
  not not_1 (not_1_out[0], enable);
  dFlipFlop dflipflop_4 (.i(_13A), .c(clock), .o(\output [13]));
  dFlipFlop dflipflop_5 (.i(_14A), .c(clock), .o(\output [14]));
  Multiplexer #(.select(2), .enable("false")) multiplexer_1 (
    .in0(\input [17]), .in1(\output [17]), .in2(1'b0), .in3(1'b0), .out(_17A), .sel({clear, not_1_out[0]}));
  dFlipFlop dflipflop_6 (.i(_12A), .c(clock), .o(\output [12]));
  dFlipFlop dflipflop_7 (.i(_11A), .c(clock), .o(\output [11]));
  Multiplexer #(.select(2), .enable("false")) multiplexer_2 (
    .in0(\input [16]), .in1(\output [16]), .in2(1'b0), .in3(1'b0), .out(_16A), .sel({clear, not_1_out[0]}));
  dFlipFlop dflipflop_8 (.i(_10A), .c(clock), .o(\output [10]));
  dFlipFlop dflipflop_9 (.i(_9A), .c(clock), .o(\output [9]));
  Multiplexer #(.select(2), .enable("false")) multiplexer_3 (
    .in0(\input [15]), .in1(\output [15]), .in2(1'b0), .in3(1'b0), .out(_15A), .sel({clear, not_1_out[0]}));
  dFlipFlop dflipflop_10 (.i(_8A), .c(clock), .o(\output [8]));
  dFlipFlop dflipflop_11 (.i(_7A), .c(clock), .o(\output [7]));
  Multiplexer #(.select(2), .enable("false")) multiplexer_4 (
    .in0(\input [14]), .in1(\output [14]), .in2(1'b0), .in3(1'b0), .out(_14A), .sel({clear, not_1_out[0]}));
  dFlipFlop dflipflop_12 (.i(_5A), .c(clock), .o(\output [5]));
  dFlipFlop dflipflop_13 (.i(_6A), .c(clock), .o(\output [6]));
  Multiplexer #(.select(2), .enable("false")) multiplexer_5 (
    .in0(\input [13]), .in1(\output [13]), .in2(1'b0), .in3(1'b0), .out(_13A), .sel({clear, not_1_out[0]}));
  dFlipFlop dflipflop_14 (.i(_4A), .c(clock), .o(\output [4]));
  dFlipFlop dflipflop_15 (.i(_3A), .c(clock), .o(\output [3]));
  Multiplexer #(.select(2), .enable("false")) multiplexer_6 (
    .in0(\input [12]), .in1(\output [12]), .in2(1'b0), .in3(1'b0), .out(_12A), .sel({clear, not_1_out[0]}));
  dFlipFlop dflipflop_16 (.i(_1A), .c(clock), .o(\output [1]));
  dFlipFlop dflipflop_17 (.i(_2A), .c(clock), .o(\output [2]));
  Multiplexer #(.select(2), .enable("false")) multiplexer_7 (
    .in0(\input [11]), .in1(\output [11]), .in2(1'b0), .in3(1'b0), .out(_11A), .sel({clear, not_1_out[0]}));
  dFlipFlop dflipflop_18 (.i(_0A), .c(clock), .o(\output [0]));
  Multiplexer #(.select(2), .enable("false")) multiplexer_8 (
    .in0(\input [10]), .in1(\output [10]), .in2(1'b0), .in3(1'b0), .out(_10A), .sel({clear, not_1_out[0]}));
  Multiplexer #(.select(2), .enable("false")) multiplexer_9 (
    .in0(\input [9]), .in1(\output [9]), .in2(1'b0), .in3(1'b0), .out(_9A), .sel({clear, not_1_out[0]}));
  Multiplexer #(.select(2), .enable("false")) multiplexer_10 (
    .in0(\input [8]), .in1(\output [8]), .in2(1'b0), .in3(1'b0), .out(_8A), .sel({clear, not_1_out[0]}));
  Multiplexer #(.select(2), .enable("false")) multiplexer_11 (
    .in0(\input [7]), .in1(\output [7]), .in2(1'b0), .in3(1'b0), .out(_7A), .sel({clear, not_1_out[0]}));
  Multiplexer #(.select(2), .enable("false")) multiplexer_12 (
    .in0(\input [6]), .in1(\output [6]), .in2(1'b0), .in3(1'b0), .out(_6A), .sel({clear, not_1_out[0]}));
  Multiplexer #(.select(2), .enable("false")) multiplexer_13 (
    .in0(\input [5]), .in1(\output [5]), .in2(1'b0), .in3(1'b0), .out(_5A), .sel({clear, not_1_out[0]}));
  Multiplexer #(.select(2), .enable("false")) multiplexer_14 (
    .in0(\input [4]), .in1(\output [4]), .in2(1'b0), .in3(1'b0), .out(_4A), .sel({clear, not_1_out[0]}));
  Multiplexer #(.select(2), .enable("false")) multiplexer_15 (
    .in0(\input [3]), .in1(\output [3]), .in2(1'b0), .in3(1'b0), .out(_3A), .sel({clear, not_1_out[0]}));
  Multiplexer #(.select(2), .enable("false")) multiplexer_16 (
    .in0(\input [2]), .in1(\output [2]), .in2(1'b0), .in3(1'b0), .out(_2A), .sel({clear, not_1_out[0]}));
  Multiplexer #(.select(2), .enable("false")) multiplexer_17 (
    .in0(\input [1]), .in1(\output [1]), .in2(1'b0), .in3(1'b0), .out(_1A), .sel({clear, not_1_out[0]}));
  Multiplexer #(.select(2), .enable("false")) multiplexer_18 (
    .in0(\input [0]), .in1(\output [0]), .in2(1'b0), .in3(1'b0), .out(_0A), .sel({clear, not_1_out[0]}));

  // Other names for the same wires on the sheet: _0 = \input [0]; _1 = \input [1]; _2 = \input [2]; _3 = \input [3];
  //   _4 = \input [4]; _5 = \input [5]; _6 = \input [6]; _7 = \input [7]; _8 = \input [8]; _9 = \input [9];
  //   _10 = \input [10]; _11 = \input [11]; _12 = \input [12]; _13 = \input [13]; _14 = \input [14];
  //   _15 = \input [15]; _16 = \input [16]; _17 = \input [17]; S = \output [0]; R = \output [1]; P = \output [2];
  //   O = \output [3]; N = \output [4]; M = \output [5]; L = \output [6]; K = \output [7]; J = \output [8];
  //   I = \output [9]; H = \output [10]; G = \output [11]; F = \output [12]; E = \output [13]; D = \output [14];
  //   C = \output [15]; B = \output [16]; A = \output [17]
endmodule

module ALU (
  input  [5:0] immediate,
  input  [17:0] i1,
  input  [17:0] i2,
  input  enable,
  input  [3:0] opcode,
  output [17:0] \output 
);

  wire [17:0] addgate_1_output, andgate_1_out_5, nandgate_1_out_3, norgate_1_out_3;

  andGate andgate_1 (.i1(i1), .i2(i2), .Immediate_value(immediate), .out_5(andgate_1_out_5), ._16_bit(opcode[2]));
  nandGate nandgate_1 (.in_1(i1), .in_2(i2), .out_3(nandgate_1_out_3));
  norGate norgate_1 (.in_1(i1), .in_2(i2), .out_3(norgate_1_out_3));
  addGate addgate_1 (.i2(i2), .Immediate_value(immediate), .i1(i1), ._16thbit(opcode[2]), .\output (addgate_1_output));
  Multiplexer #(.select(4), .width(18)) multiplexer_1 (
    .in0(addgate_1_output), .in1(andgate_1_out_5), .in2(nandgate_1_out_3), .in3(norgate_1_out_3),
    .in4(addgate_1_output), .in5(andgate_1_out_5), .out(\output ), .sel(opcode), .en(enable));  // open: in6, in7, in8, in9, in10, in11, in12, in13, in14, in15

  // Other names for the same wires on the sheet: _16thbit = opcode[2]
endmodule

module extendImmediateValue (
  input  [5:0] in_1,
  output [17:0] out_2
);

  xnor xnor_1 (out_2[17], 1'b1, in_1[5]);

  assign out_2[16:0] = {{12{out_2[17]}}, in_1[4:0]};
endmodule

module addGate (
  input  [17:0] i2,
  input  _16thbit,
  input  [17:0] i1,
  input  [5:0] Immediate_value,
  output [17:0] \output 
);

  wire _2nd13, fulladder_1_carryout, fulladder_3_carryout, fulladder_4_carryout, fulladder_5_carryout,
       fulladder_6_carryout, fulladder_7_carryout, fulladder_8_carryout, fulladder_9_carryout,
       fulladder_10_carryout, fulladder_11_carryout, fulladder_12_carryout, fulladder_13_carryout,
       fulladder_14_carryout, fulladder_15_carryout, fulladder_16_carryout, fulladder_17_carryout,
       halfadder_1_carryout;
  wire [17:0] extendimmediatevalue_1_out_2, multiplexer_1_out;

  fullAdder fulladder_1 (
    .CarryIn(fulladder_4_carryout), .i1(i1[16]), .i2(multiplexer_1_out[16]), .CarryOut(fulladder_1_carryout),
    .S(\output [16]));
  fullAdder fulladder_2 (
    .CarryIn(fulladder_1_carryout), .i1(i1[17]), .i2(multiplexer_1_out[17]), .S(\output [17]));  // open: CarryOut
  extendImmediateValue extendimmediatevalue_1 (.in_1(Immediate_value), .out_2(extendimmediatevalue_1_out_2));
  fullAdder fulladder_3 (
    .CarryIn(fulladder_5_carryout), .i1(i1[14]), .i2(multiplexer_1_out[14]), .CarryOut(fulladder_3_carryout),
    .S(\output [14]));
  fullAdder fulladder_4 (
    .CarryIn(fulladder_3_carryout), .i1(i1[15]), .i2(multiplexer_1_out[15]), .CarryOut(fulladder_4_carryout),
    .S(\output [15]));
  fullAdder fulladder_5 (
    .CarryIn(fulladder_7_carryout), .i1(i1[13]), .i2(_2nd13), .CarryOut(fulladder_5_carryout),
    .S(\output [13]));
  Multiplexer #(.width(18)) multiplexer_1 (
    .in0(i2), .in1(extendimmediatevalue_1_out_2),
    .out({multiplexer_1_out[17:14], _2nd13, multiplexer_1_out[12:0]}), .sel(_16thbit), .en(1'b1));
  fullAdder fulladder_6 (
    .CarryIn(fulladder_8_carryout), .i1(i1[11]), .i2(multiplexer_1_out[11]), .CarryOut(fulladder_6_carryout),
    .S(\output [11]));
  fullAdder fulladder_7 (
    .CarryIn(fulladder_6_carryout), .i1(i1[12]), .i2(multiplexer_1_out[12]), .CarryOut(fulladder_7_carryout),
    .S(\output [12]));
  fullAdder fulladder_8 (
    .CarryIn(fulladder_10_carryout), .i1(i1[10]), .i2(multiplexer_1_out[10]),
    .CarryOut(fulladder_8_carryout), .S(\output [10]));
  fullAdder fulladder_9 (
    .CarryIn(fulladder_12_carryout), .i1(i1[8]), .i2(multiplexer_1_out[8]), .CarryOut(fulladder_9_carryout),
    .S(\output [8]));
  fullAdder fulladder_10 (
    .CarryIn(fulladder_9_carryout), .i1(i1[9]), .i2(multiplexer_1_out[9]), .CarryOut(fulladder_10_carryout),
    .S(\output [9]));
  fullAdder fulladder_11 (
    .CarryIn(fulladder_13_carryout), .i1(i1[6]), .i2(multiplexer_1_out[6]), .CarryOut(fulladder_11_carryout),
    .S(\output [6]));
  fullAdder fulladder_12 (
    .CarryIn(fulladder_11_carryout), .i1(i1[7]), .i2(multiplexer_1_out[7]), .CarryOut(fulladder_12_carryout),
    .S(\output [7]));
  fullAdder fulladder_13 (
    .CarryIn(fulladder_15_carryout), .i1(i1[5]), .i2(multiplexer_1_out[5]), .CarryOut(fulladder_13_carryout),
    .S(\output [5]));
  fullAdder fulladder_14 (
    .CarryIn(fulladder_16_carryout), .i1(i1[3]), .i2(multiplexer_1_out[3]), .CarryOut(fulladder_14_carryout),
    .S(\output [3]));
  fullAdder fulladder_15 (
    .CarryIn(fulladder_14_carryout), .i1(i1[4]), .i2(multiplexer_1_out[4]), .CarryOut(fulladder_15_carryout),
    .S(\output [4]));
  fullAdder fulladder_16 (
    .CarryIn(fulladder_17_carryout), .i1(i1[2]), .i2(multiplexer_1_out[2]), .CarryOut(fulladder_16_carryout),
    .S(\output [2]));
  halfAdder halfadder_1 (.i2(i1[0]), .i1(multiplexer_1_out[0]), .CarryOut(halfadder_1_carryout), .s(\output [0]));
  fullAdder fulladder_17 (
    .CarryIn(halfadder_1_carryout), .i1(i1[1]), .i2(multiplexer_1_out[1]), .CarryOut(fulladder_17_carryout),
    .S(\output [1]));

  // Other names for the same wires on the sheet: _1 = i1[13]
endmodule

module extendAddressValue (
  input  [9:0] in_1,
  output [17:0] out_2
);

  xnor xnor_1 (out_2[17], 1'b1, in_1[9]);

  assign out_2[16:0] = {{8{out_2[17]}}, in_1[8:0]};
endmodule

module halfCmp (
  input  in_1,
  input  in_2,
  output GT,
  output LT,
  output EQ
);

  wire not_1_out, not_2_out;

  not not_1 (not_1_out, in_1);
  and and_1 (GT, in_2, not_1_out);
  not not_2 (not_2_out, in_2);
  and and_2 (LT, not_2_out, in_1);
  xnor xnor_1 (EQ, in_2, in_1);
endmodule

module fullCmp (
  input  A,
  input  B,
  input  GT,
  input  LT,
  input  EQ,
  output EQ_2,
  output GT_2,
  output LT_2
);

  wire and_1_out, and_2_out, and_3_out, and_4_out, halfcmp_1_eq, halfcmp_1_gt, halfcmp_1_lt;

  halfCmp halfcmp_1 (.in_2(A), .in_1(B), .GT(halfcmp_1_gt), .LT(halfcmp_1_lt), .EQ(halfcmp_1_eq));
  and and_1 (and_1_out, halfcmp_1_gt, ~GT, EQ);  // AND_Gate
  and and_2 (and_2_out, GT, ~EQ);  // AND_Gate
  or or_1 (GT_2, and_1_out, and_2_out);
  and and_3 (and_3_out, halfcmp_1_lt, ~LT, EQ);  // AND_Gate
  and and_4 (and_4_out, LT, ~EQ);  // AND_Gate
  or or_2 (LT_2, and_3_out, and_4_out);
  and and_5 (EQ_2, halfcmp_1_eq, EQ);
endmodule

// CMP
module subtractGate (
  input  [17:0] i1,
  input  [17:0] i2,
  input  clock,
  input  isCmp,
  output carry_flag,
  output zero_flag
);

  wire _17th, nor_1_out;
  wire [16:0] addgate_1_output;
  wire [17:0] addgate_2_output, extend1to18_1_out_2, not_14_out;

  addGate addgate_1 (
    .i2(addgate_2_output), .i1(i1), ._16thbit(1'b0), .\output ({_17th, addgate_1_output}));  // open: Immediate_value
  not not_1 (not_14_out[16], i2[16]);
  not not_2 (not_14_out[17], i2[17]);
  not not_3 (not_14_out[14], i2[14]);
  not not_4 (not_14_out[15], i2[15]);
  not not_5 (not_14_out[8], i2[8]);
  not not_6 (not_14_out[12], i2[12]);
  not not_7 (not_14_out[10], i2[10]);
  not not_8 (not_14_out[13], i2[13]);
  not not_9 (not_14_out[11], i2[11]);
  not not_10 (not_14_out[9], i2[9]);
  not not_11 (not_14_out[6], i2[6]);
  not not_12 (not_14_out[2], i2[2]);
  not not_13 (not_14_out[5], i2[5]);
  not not_14 (not_14_out[0], i2[0]);
  not not_15 (not_14_out[7], i2[7]);
  not not_16 (not_14_out[3], i2[3]);
  not not_17 (not_14_out[4], i2[4]);
  not not_18 (not_14_out[1], i2[1]);
  extend1to18 extend1to18_1 (.in_1(1'b1), .out_2(extend1to18_1_out_2));
  addGate addgate_2 (
    .i2(extend1to18_1_out_2), .i1(not_14_out), ._16thbit(1'b0), .\output (addgate_2_output));  // open: Immediate_value
  nor nor_1 (nor_1_out, addgate_1_output[0], addgate_1_output[1], addgate_1_output[2], addgate_1_output[3], addgate_1_output[4], addgate_1_output[5], addgate_1_output[6], addgate_1_output[7], addgate_1_output[8], addgate_1_output[9], addgate_1_output[10], addgate_1_output[11], addgate_1_output[12], addgate_1_output[13], addgate_1_output[14], addgate_1_output[15], addgate_1_output[16], _17th);
  Register #(.width(1)) register_1 (.D(_17th), .en(isCmp), .Q(carry_flag), .clk(clock), .clr(1'b0));
  Register #(.width(1)) register_2 (.D(nor_1_out), .en(isCmp), .Q(zero_flag), .clk(clock), .clr(1'b0));
endmodule

module extend1to18 (
  input  in_1,
  output [17:0] out_2
);

  not not_1 (out_2[17], 1'b1);

  assign out_2[16:0] = {{16{out_2[17]}}, in_1};
endmodule

module Control_Unit (
  input  [17:0] in_1,
  output [1:0] NORCODE__NANDCODE_ANDCODE__ADDCODE,
  output [3:0] OP2__SRC2,
  output [17:0] IMM__18,
  output isCMP,
  output MemoryRead,
  output MemoryWrite,
  output [3:0] OPCODE,
  output Register_Write_Enable,
  output isALU,
  output isJMP,
  output [3:0] OP1,
  output [2:0] Cmp_Jump_Code,
  output [9:0] ADDRESS,
  output [3:0] Source_1,
  output [3:0] Source_2,
  output [5:0] IMMEDIATE,
  output [3:0] JUMPCODE__OP1__source1_ST__destination,
  output isCmpJump
);

  wire ADD, ADDI, AND, ANDI, decoder_1_out15, JA, JAE, JB, JBE, JE, NAND, NOR;

  extendImmediateValue extendimmediatevalue_1 (.in_1(in_1[5:0]), .out_2(IMM__18));
  or or_1 (Register_Write_Enable, isALU, MemoryRead);
  Decoder #(.select(4), .enable("false")) decoder_1 (
    .out0(ADD), .out1(AND), .out2(NAND), .out3(NOR), .out4(ADDI), .out5(ANDI), .out6(MemoryRead),
    .out7(MemoryWrite), .out8(isCMP), .out9(isJMP), .out10(JE), .out11(JA), .out12(JB), .out13(JAE),
    .out14(JBE), .out15(decoder_1_out15), .sel(in_1[17:14]));
  or or_2 (isALU, ADD, ADDI, AND, ANDI, NAND, NOR);
  Multiplexer #(.select(4), .width(3)) multiplexer_1 (
    .in10(3'b000), .in11(3'b001), .in12(3'b010), .in13(3'b011), .in14(3'b100), .out(Cmp_Jump_Code),
    .sel(in_1[17:14]), .en(isCmpJump));  // open: in0, in1, in2, in3, in4, in5, in6, in7, in8, in9, in15
  or or_3 (isCmpJump, JE, JA, JB, JAE, JBE);
  Decoder #(.select(4), .enable("false")) decoder_2 ();  // open: out0, out1, out2, out3, out4, out5, out6, out7, out8, out9, out10, out11, out12, out13, out14, out15, sel

  assign ADDRESS = in_1[9:0];
  assign IMMEDIATE = in_1[5:0];
  assign JUMPCODE__OP1__source1_ST__destination = in_1[13:10];
  assign NORCODE__NANDCODE_ANDCODE__ADDCODE = in_1[5:4];
  assign OP1 = in_1[13:10];
  assign OP2__SRC2 = in_1[3:0];
  assign OPCODE = in_1[17:14];
  assign Source_1 = in_1[9:6];
  assign Source_2 = in_1[3:0];

  // Other names for the same wires on the sheet: OP2[3:0] = in_1[3:0]; source2[3:0] = in_1[3:0];
  //   ADDCODE[1:0] = in_1[5:4]; ANDCODE[1:0] = in_1[5:4];
  //   CMPCODE[5:0] = {in_1[4], in_1[5], in_1[6], in_1[7], in_1[8], in_1[9]}; NANDCODE[1:0] = in_1[5:4];
  //   NORCODE[1:0] = in_1[5:4]; source1[3:0] = in_1[9:6]; CMP = isCMP; CmpJumpCode[2:0] = Cmp_Jump_Code; JUMP = isJMP;
  //   LD = MemoryRead; destination[3:0] = in_1[13:10]; JUMPCODE[3:0] = in_1[13:10]; source1_ST[3:0] = in_1[13:10];
  //   ST = MemoryWrite

  // Notes on the sheet:
  //   JUMPCODE/ OP1/ source1_ST/ destination hangis
  //   olduğunu opcode yardımıyla ayırıyor
endmodule

module counter (
  input  [9:0] jumpValue,
  input  isJump,
  input  clock,
  input  clear,
  output [9:0] \output 
);

  wire [9:0] multiplexer_1_out, n10bitadder_1_output;

  Multiplexer #(.width(10), .enable("false")) multiplexer_1 (
    .in0(10'h1), .in1(jumpValue), .out(multiplexer_1_out), .sel(isJump));
  _10bitadder u_10bitadder_1 (.i1(\output ), .i2(multiplexer_1_out), .\output (n10bitadder_1_output));
  Register #(.width(10)) register_1 (.D(n10bitadder_1_output), .en(1'b1), .Q(\output ), .clk(clock), .clr(clear));
endmodule

module registerFile (
  input  [3:0] Read_Register_1,
  input  [3:0] Read_Register_2,
  input  [17:0] data_for_write,
  input  [3:0] Write_Register,
  input  Write_Enable,
  input  Clock,
  output [17:0] R0,
  output [17:0] R1,
  output [17:0] R2,
  output [17:0] R3,
  output [17:0] Register_Output_1,
  output [17:0] R4,
  output [17:0] Register_Output_2,
  output [17:0] R5,
  output [17:0] R6,
  output [17:0] R7,
  output [17:0] R8,
  output [17:0] R9,
  output [17:0] R10,
  output [17:0] R11,
  output [17:0] R12,
  output [17:0] R13,
  output [17:0] R14,
  output [17:0] R15
);

  wire controlled_buffer_1_out, controlled_buffer_2_out, controlled_buffer_3_out, controlled_buffer_4_out,
       controlled_buffer_5_out, controlled_buffer_6_out, controlled_buffer_7_out, controlled_buffer_8_out,
       controlled_buffer_9_out, controlled_buffer_10_out, controlled_buffer_11_out, controlled_buffer_12_out,
       controlled_buffer_13_out, controlled_buffer_14_out, controlled_buffer_15_out,
       controlled_buffer_16_out, decoder_1_out0, decoder_1_out1, decoder_1_out2, decoder_1_out3,
       decoder_1_out4, decoder_1_out5, decoder_1_out6, decoder_1_out7, decoder_1_out8, decoder_1_out9,
       decoder_1_out10, decoder_1_out11, decoder_1_out12, decoder_1_out13, decoder_1_out14, decoder_1_out15,
       decoder_2_out0, decoder_2_out1, decoder_2_out2, decoder_2_out3, decoder_2_out4, decoder_2_out5,
       decoder_2_out6, decoder_2_out7, decoder_2_out8, decoder_2_out9, decoder_2_out10, decoder_2_out11,
       decoder_2_out12, decoder_2_out13, decoder_2_out14, decoder_2_out15, decoder_3_out0, decoder_3_out1,
       decoder_3_out2, decoder_3_out3, decoder_3_out4, decoder_3_out5, decoder_3_out6, decoder_3_out7,
       decoder_3_out8, decoder_3_out9, decoder_3_out10, decoder_3_out11, decoder_3_out12, decoder_3_out13,
       decoder_3_out14, decoder_3_out15, multiplexer_2_out, multiplexer_3_out, multiplexer_4_out,
       multiplexer_5_out, multiplexer_6_out, multiplexer_7_out, multiplexer_8_out, multiplexer_9_out,
       multiplexer_10_out, multiplexer_11_out, multiplexer_12_out, multiplexer_13_out, multiplexer_14_out,
       multiplexer_15_out, multiplexer_16_out, multiplexer_17_out;
  wire [17:0] multiplexer_1_out;

  Decoder #(.select(4), .enable("false")) decoder_1 (
    .out0(decoder_1_out0), .out1(decoder_1_out1), .out2(decoder_1_out2), .out3(decoder_1_out3),
    .out4(decoder_1_out4), .out5(decoder_1_out5), .out6(decoder_1_out6), .out7(decoder_1_out7),
    .out8(decoder_1_out8), .out9(decoder_1_out9), .out10(decoder_1_out10), .out11(decoder_1_out11),
    .out12(decoder_1_out12), .out13(decoder_1_out13), .out14(decoder_1_out14), .out15(decoder_1_out15),
    .sel(Read_Register_1));
  Decoder #(.select(4), .enable("false")) decoder_2 (
    .out0(decoder_2_out0), .out1(decoder_2_out1), .out2(decoder_2_out2), .out3(decoder_2_out3),
    .out4(decoder_2_out4), .out5(decoder_2_out5), .out6(decoder_2_out6), .out7(decoder_2_out7),
    .out8(decoder_2_out8), .out9(decoder_2_out9), .out10(decoder_2_out10), .out11(decoder_2_out11),
    .out12(decoder_2_out12), .out13(decoder_2_out13), .out14(decoder_2_out14), .out15(decoder_2_out15),
    .sel(Read_Register_2));
  Decoder #(.select(4), .enable("false")) decoder_3 (
    .out0(decoder_3_out0), .out1(decoder_3_out1), .out2(decoder_3_out2), .out3(decoder_3_out3),
    .out4(decoder_3_out4), .out5(decoder_3_out5), .out6(decoder_3_out6), .out7(decoder_3_out7),
    .out8(decoder_3_out8), .out9(decoder_3_out9), .out10(decoder_3_out10), .out11(decoder_3_out11),
    .out12(decoder_3_out12), .out13(decoder_3_out13), .out14(decoder_3_out14), .out15(decoder_3_out15),
    .sel(Write_Register));
  assign controlled_buffer_1_out = Write_Enable ? decoder_3_out0 : 1'bz;  // Controlled_Buffer controlled_buffer_1
  assign controlled_buffer_2_out = Write_Enable ? decoder_3_out1 : 1'bz;  // Controlled_Buffer controlled_buffer_2
  assign controlled_buffer_3_out = Write_Enable ? decoder_3_out2 : 1'bz;  // Controlled_Buffer controlled_buffer_3
  assign controlled_buffer_4_out = Write_Enable ? decoder_3_out3 : 1'bz;  // Controlled_Buffer controlled_buffer_4
  assign controlled_buffer_5_out = Write_Enable ? decoder_3_out4 : 1'bz;  // Controlled_Buffer controlled_buffer_5
  assign controlled_buffer_6_out = Write_Enable ? decoder_3_out5 : 1'bz;  // Controlled_Buffer controlled_buffer_6
  assign controlled_buffer_7_out = Write_Enable ? decoder_3_out6 : 1'bz;  // Controlled_Buffer controlled_buffer_7
  assign controlled_buffer_8_out = Write_Enable ? decoder_3_out7 : 1'bz;  // Controlled_Buffer controlled_buffer_8
  assign controlled_buffer_9_out = Write_Enable ? decoder_3_out8 : 1'bz;  // Controlled_Buffer controlled_buffer_9
  assign controlled_buffer_10_out = Write_Enable ? decoder_3_out9 : 1'bz;  // Controlled_Buffer controlled_buffer_10
  assign controlled_buffer_11_out = Write_Enable ? decoder_3_out10 : 1'bz;  // Controlled_Buffer controlled_buffer_11
  assign controlled_buffer_12_out = Write_Enable ? decoder_3_out11 : 1'bz;  // Controlled_Buffer controlled_buffer_12
  assign controlled_buffer_13_out = Write_Enable ? decoder_3_out12 : 1'bz;  // Controlled_Buffer controlled_buffer_13
  assign controlled_buffer_14_out = Write_Enable ? decoder_3_out13 : 1'bz;  // Controlled_Buffer controlled_buffer_14
  assign controlled_buffer_15_out = Write_Enable ? decoder_3_out14 : 1'bz;  // Controlled_Buffer controlled_buffer_15
  assign controlled_buffer_16_out = Write_Enable ? decoder_3_out15 : 1'bz;  // Controlled_Buffer controlled_buffer_16
  Multiplexer #(.width(18), .enable("false")) multiplexer_1 (
    .in0({18{1'b0}}), .in1(data_for_write), .out(multiplexer_1_out), .sel(Write_Enable));
  Multiplexer #(.enable("false")) multiplexer_2 (
    .in0(1'b0), .in1(controlled_buffer_1_out), .out(multiplexer_2_out), .sel(Write_Enable));
  Multiplexer #(.enable("false")) multiplexer_3 (
    .in0(1'b0), .in1(controlled_buffer_2_out), .out(multiplexer_3_out), .sel(Write_Enable));
  Multiplexer #(.enable("false")) multiplexer_4 (
    .in0(1'b0), .in1(controlled_buffer_3_out), .out(multiplexer_4_out), .sel(Write_Enable));
  Multiplexer #(.enable("false")) multiplexer_5 (
    .in0(1'b0), .in1(controlled_buffer_4_out), .out(multiplexer_5_out), .sel(Write_Enable));
  Multiplexer #(.enable("false")) multiplexer_6 (
    .in0(1'b0), .in1(controlled_buffer_5_out), .out(multiplexer_6_out), .sel(Write_Enable));
  Multiplexer #(.enable("false")) multiplexer_7 (
    .in0(1'b0), .in1(controlled_buffer_6_out), .out(multiplexer_7_out), .sel(Write_Enable));
  Multiplexer #(.enable("false")) multiplexer_8 (
    .in0(1'b0), .in1(controlled_buffer_7_out), .out(multiplexer_8_out), .sel(Write_Enable));
  Multiplexer #(.enable("false")) multiplexer_9 (
    .in0(1'b0), .in1(controlled_buffer_8_out), .out(multiplexer_9_out), .sel(Write_Enable));
  Multiplexer #(.enable("false")) multiplexer_10 (
    .in0(1'b0), .in1(controlled_buffer_9_out), .out(multiplexer_10_out), .sel(Write_Enable));
  Multiplexer #(.enable("false")) multiplexer_11 (
    .in0(1'b0), .in1(controlled_buffer_10_out), .out(multiplexer_11_out), .sel(Write_Enable));
  Multiplexer #(.enable("false")) multiplexer_12 (
    .in0(1'b0), .in1(controlled_buffer_11_out), .out(multiplexer_12_out), .sel(Write_Enable));
  Multiplexer #(.enable("false")) multiplexer_13 (
    .in0(1'b0), .in1(controlled_buffer_12_out), .out(multiplexer_13_out), .sel(Write_Enable));
  Multiplexer #(.enable("false")) multiplexer_14 (
    .in0(1'b0), .in1(controlled_buffer_13_out), .out(multiplexer_14_out), .sel(Write_Enable));
  Multiplexer #(.enable("false")) multiplexer_15 (
    .in0(1'b0), .in1(controlled_buffer_14_out), .out(multiplexer_15_out), .sel(Write_Enable));
  Multiplexer #(.enable("false")) multiplexer_16 (
    .in0(1'b0), .in1(controlled_buffer_15_out), .out(multiplexer_16_out), .sel(Write_Enable));
  Multiplexer #(.enable("false")) multiplexer_17 (
    .in0(1'b0), .in1(controlled_buffer_16_out), .out(multiplexer_17_out), .sel(Write_Enable));
  register register_1 (
    .enable(multiplexer_2_out), .clear(1'b0), .clock(Clock), .\input (multiplexer_1_out), .\output (R0));
  register register_2 (
    .enable(multiplexer_3_out), .clear(1'b0), .clock(Clock), .\input (multiplexer_1_out), .\output (R1));
  register register_3 (
    .enable(multiplexer_4_out), .clear(1'b0), .clock(Clock), .\input (multiplexer_1_out), .\output (R2));
  register register_4 (
    .enable(multiplexer_5_out), .clear(1'b0), .clock(Clock), .\input (multiplexer_1_out), .\output (R3));
  register register_5 (
    .enable(multiplexer_6_out), .clear(1'b0), .clock(Clock), .\input (multiplexer_1_out), .\output (R4));
  register register_6 (
    .enable(multiplexer_7_out), .clear(1'b0), .clock(Clock), .\input (multiplexer_1_out), .\output (R5));
  register register_7 (
    .enable(multiplexer_8_out), .clear(1'b0), .clock(Clock), .\input (multiplexer_1_out), .\output (R6));
  register register_8 (
    .enable(multiplexer_9_out), .clear(1'b0), .clock(Clock), .\input (multiplexer_1_out), .\output (R7));
  register register_9 (
    .enable(multiplexer_10_out), .clear(1'b0), .clock(Clock), .\input (multiplexer_1_out), .\output (R8));
  register register_10 (
    .enable(multiplexer_11_out), .clear(1'b0), .clock(Clock), .\input (multiplexer_1_out), .\output (R9));
  register register_11 (
    .enable(multiplexer_12_out), .clear(1'b0), .clock(Clock), .\input (multiplexer_1_out), .\output (R10));
  register register_12 (
    .enable(multiplexer_13_out), .clear(1'b0), .clock(Clock), .\input (multiplexer_1_out), .\output (R11));
  register register_13 (
    .enable(multiplexer_14_out), .clear(1'b0), .clock(Clock), .\input (multiplexer_1_out), .\output (R12));
  register register_14 (
    .enable(multiplexer_15_out), .clear(1'b0), .clock(Clock), .\input (multiplexer_1_out), .\output (R13));
  register register_15 (
    .enable(multiplexer_16_out), .clear(1'b0), .clock(Clock), .\input (multiplexer_1_out), .\output (R14));
  register register_16 (
    .enable(multiplexer_17_out), .clear(1'b0), .clock(Clock), .\input (multiplexer_1_out), .\output (R15));
  assign Register_Output_1 = decoder_1_out0 ? R0 : 18'bz;  // Controlled_Buffer controlled_buffer_17
  assign Register_Output_2 = decoder_2_out0 ? R0 : 18'bz;  // Controlled_Buffer controlled_buffer_18
  assign Register_Output_1 = decoder_1_out1 ? R1 : 18'bz;  // Controlled_Buffer controlled_buffer_19
  assign Register_Output_2 = decoder_2_out1 ? R1 : 18'bz;  // Controlled_Buffer controlled_buffer_20
  assign Register_Output_1 = decoder_1_out2 ? R2 : 18'bz;  // Controlled_Buffer controlled_buffer_21
  assign Register_Output_2 = decoder_2_out2 ? R2 : 18'bz;  // Controlled_Buffer controlled_buffer_22
  assign Register_Output_1 = decoder_1_out3 ? R3 : 18'bz;  // Controlled_Buffer controlled_buffer_23
  assign Register_Output_2 = decoder_2_out3 ? R3 : 18'bz;  // Controlled_Buffer controlled_buffer_24
  assign Register_Output_1 = decoder_1_out4 ? R4 : 18'bz;  // Controlled_Buffer controlled_buffer_25
  assign Register_Output_2 = decoder_2_out4 ? R4 : 18'bz;  // Controlled_Buffer controlled_buffer_26
  assign Register_Output_1 = decoder_1_out5 ? R5 : 18'bz;  // Controlled_Buffer controlled_buffer_27
  assign Register_Output_2 = decoder_2_out5 ? R5 : 18'bz;  // Controlled_Buffer controlled_buffer_28
  assign Register_Output_1 = decoder_1_out6 ? R6 : 18'bz;  // Controlled_Buffer controlled_buffer_29
  assign Register_Output_2 = decoder_2_out6 ? R6 : 18'bz;  // Controlled_Buffer controlled_buffer_30
  assign Register_Output_1 = decoder_1_out7 ? R7 : 18'bz;  // Controlled_Buffer controlled_buffer_31
  assign Register_Output_2 = decoder_2_out7 ? R7 : 18'bz;  // Controlled_Buffer controlled_buffer_32
  assign Register_Output_1 = decoder_1_out8 ? R8 : 18'bz;  // Controlled_Buffer controlled_buffer_33
  assign Register_Output_2 = decoder_2_out8 ? R8 : 18'bz;  // Controlled_Buffer controlled_buffer_34
  assign Register_Output_1 = decoder_1_out9 ? R9 : 18'bz;  // Controlled_Buffer controlled_buffer_35
  assign Register_Output_2 = decoder_2_out9 ? R9 : 18'bz;  // Controlled_Buffer controlled_buffer_36
  assign Register_Output_1 = decoder_1_out10 ? R10 : 18'bz;  // Controlled_Buffer controlled_buffer_37
  assign Register_Output_2 = decoder_2_out10 ? R10 : 18'bz;  // Controlled_Buffer controlled_buffer_38
  assign Register_Output_1 = decoder_1_out11 ? R11 : 18'bz;  // Controlled_Buffer controlled_buffer_39
  assign Register_Output_2 = decoder_2_out11 ? R11 : 18'bz;  // Controlled_Buffer controlled_buffer_40
  assign Register_Output_1 = decoder_1_out12 ? R12 : 18'bz;  // Controlled_Buffer controlled_buffer_41
  assign Register_Output_2 = decoder_2_out12 ? R12 : 18'bz;  // Controlled_Buffer controlled_buffer_42
  assign Register_Output_1 = decoder_1_out13 ? R13 : 18'bz;  // Controlled_Buffer controlled_buffer_43
  assign Register_Output_2 = decoder_2_out13 ? R13 : 18'bz;  // Controlled_Buffer controlled_buffer_44
  assign Register_Output_1 = decoder_1_out14 ? R14 : 18'bz;  // Controlled_Buffer controlled_buffer_45
  assign Register_Output_2 = decoder_2_out14 ? R14 : 18'bz;  // Controlled_Buffer controlled_buffer_46
  assign Register_Output_1 = decoder_1_out15 ? R15 : 18'bz;  // Controlled_Buffer controlled_buffer_47
  assign Register_Output_2 = decoder_2_out15 ? R15 : 18'bz;  // Controlled_Buffer controlled_buffer_48
endmodule

module fsm (
  input  [3:0] in_1,
  input  in_2,
  input  in_3,
  input  in_4,
  input  in_5,
  input  in_6,
  input  in_7,
  input  in_8,
  input  in_9,
  input  in_10,
  input  in_11,
  input  [3:0] in_12,
  input  in_13,
  input  in_14,
  input  in_15,
  input  in_16,
  input  in_17,
  output [17:0] out_18
);

  wire isALU;
  wire [17:0] Read_Source_Register_1, Read_Source_Register_2;

  ALU alu_1 (
    .i1(Read_Source_Register_1), .i2(Read_Source_Register_2), .\output (out_18), .enable(isALU),
    .opcode(in_12));  // open: immediate

  // Other names for the same wires on the sheet: ADD = in_2; ADDI = in_6; AND = in_3; ANDI = in_7; CMP = in_10;
  //   JA = in_14; JAE = in_16; JB = in_15; JBE = in_17; JE = in_13; JUMP = in_11; LD = in_8; NAND = in_4; NOR = in_5;
  //   _16_15_14[2:0] = in_1[2:0]; OPCODE[3:0] = in_1; _17th = in_1[3]; ST = in_9

  // Notes on the sheet:
  //   17. biti 0 ise ve diğer 3 bit (16,,15,14) 1 ise
  //   ST demektir ve registerdan read işlemi yapılacaktır
  //   17. biti 1 ise ve diğer bitler 0 ise CMP işlemidir, read basesi işleme girecektir
  //   diğer bitler 0 ise JUMP işlemidir count base'si devreye girecektir
  //   diğer tarafta ise 14. bit 0 ise LD işlemi yapılacaktır.
  //   14. bit 0 değilse ALU işlemi olacaktır
  //   Burada da 16. bite bakılarak IMMEDIATE value ile mi işlem yapılacak karar verilecektir.
endmodule

module _10bitadder (
  input  [9:0] i1,
  input  [9:0] i2,
  output [9:0] \output 
);

  wire fulladder_2_carryout, fulladder_3_carryout, fulladder_4_carryout, fulladder_5_carryout,
       fulladder_6_carryout, fulladder_7_carryout, fulladder_8_carryout, fulladder_9_carryout,
       halfadder_1_carryout;

  fullAdder fulladder_1 (.CarryIn(fulladder_3_carryout), .i1(i2[9]), .i2(i1[9]), .S(\output [9]));  // open: CarryOut
  fullAdder fulladder_2 (
    .CarryIn(fulladder_5_carryout), .i1(i2[7]), .i2(i1[7]), .CarryOut(fulladder_2_carryout), .S(\output [7]));
  fullAdder fulladder_3 (
    .CarryIn(fulladder_2_carryout), .i1(i2[8]), .i2(i1[8]), .CarryOut(fulladder_3_carryout), .S(\output [8]));
  fullAdder fulladder_4 (
    .CarryIn(fulladder_7_carryout), .i1(i2[5]), .i2(i1[5]), .CarryOut(fulladder_4_carryout), .S(\output [5]));
  fullAdder fulladder_5 (
    .CarryIn(fulladder_4_carryout), .i1(i2[6]), .i2(i1[6]), .CarryOut(fulladder_5_carryout), .S(\output [6]));
  fullAdder fulladder_6 (
    .CarryIn(fulladder_8_carryout), .i1(i2[3]), .i2(i1[3]), .CarryOut(fulladder_6_carryout), .S(\output [3]));
  fullAdder fulladder_7 (
    .CarryIn(fulladder_6_carryout), .i1(i2[4]), .i2(i1[4]), .CarryOut(fulladder_7_carryout), .S(\output [4]));
  fullAdder fulladder_8 (
    .CarryIn(fulladder_9_carryout), .i1(i2[2]), .i2(i1[2]), .CarryOut(fulladder_8_carryout), .S(\output [2]));
  fullAdder fulladder_9 (
    .CarryIn(halfadder_1_carryout), .i1(i2[1]), .i2(i1[1]), .CarryOut(fulladder_9_carryout), .S(\output [1]));
  halfAdder halfadder_1 (.i2(i2[0]), .i1(i1[0]), .CarryOut(halfadder_1_carryout), .s(\output [0]));

  // Other names for the same wires on the sheet: _10 = i1[0]; _11 = i1[1]; _12 = i1[2]; _13 = i1[3]; _14 = i1[4];
  //   _15 = i1[5]; _16 = i1[6]; _17 = i1[7]; _18 = i1[8]; _19 = i1[9]; _20 = i2[0]; _21 = i2[1]; _22 = i2[2];
  //   _23 = i2[3]; _24 = i2[4]; _25 = i2[5]; _26 = i2[6]; _27 = i2[7]; _28 = i2[8]; _29 = i2[9]
endmodule

module _10bitRegister (
  input  [9:0] \input ,
  input  clock,
  input  enable,
  input  clear,
  output [9:0] \output 
);

  wire _0A, _1A, _2A, _3A, _4A, _5A, _6A, _7A, _8A, _9A;
  wire [0:0] not_1_out;

  dFlipFlop dflipflop_1 (.i(_9A), .c(clock), .o(\output [9]));
  dFlipFlop dflipflop_2 (.i(_7A), .c(clock), .o(\output [7]));
  dFlipFlop dflipflop_3 (.i(_8A), .c(clock), .o(\output [8]));
  dFlipFlop dflipflop_4 (.i(_5A), .c(clock), .o(\output [5]));
  dFlipFlop dflipflop_5 (.i(_6A), .c(clock), .o(\output [6]));
  dFlipFlop dflipflop_6 (.i(_4A), .c(clock), .o(\output [4]));
  dFlipFlop dflipflop_7 (.i(_3A), .c(clock), .o(\output [3]));
  dFlipFlop dflipflop_8 (.i(_1A), .c(clock), .o(\output [1]));
  dFlipFlop dflipflop_9 (.i(_2A), .c(clock), .o(\output [2]));
  dFlipFlop dflipflop_10 (.i(_0A), .c(clock), .o(\output [0]));
  not not_1 (not_1_out[0], enable);
  Multiplexer #(.select(2), .enable("false")) multiplexer_1 (
    .in0(\input [9]), .in1(\output [9]), .in2(1'b0), .in3(1'b0), .out(_9A), .sel({clear, not_1_out[0]}));
  Multiplexer #(.select(2), .enable("false")) multiplexer_2 (
    .in0(\input [8]), .in1(\output [8]), .in2(1'b0), .in3(1'b0), .out(_8A), .sel({clear, not_1_out[0]}));
  Multiplexer #(.select(2), .enable("false")) multiplexer_3 (
    .in0(\input [7]), .in1(\output [7]), .in2(1'b0), .in3(1'b0), .out(_7A), .sel({clear, not_1_out[0]}));
  Multiplexer #(.select(2), .enable("false")) multiplexer_4 (
    .in0(\input [6]), .in1(\output [6]), .in2(1'b0), .in3(1'b0), .out(_6A), .sel({clear, not_1_out[0]}));
  Multiplexer #(.select(2), .enable("false")) multiplexer_5 (
    .in0(\input [5]), .in1(\output [5]), .in2(1'b0), .in3(1'b0), .out(_5A), .sel({clear, not_1_out[0]}));
  Multiplexer #(.select(2), .enable("false")) multiplexer_6 (
    .in0(\input [4]), .in1(\output [4]), .in2(1'b0), .in3(1'b0), .out(_4A), .sel({clear, not_1_out[0]}));
  Multiplexer #(.select(2), .enable("false")) multiplexer_7 (
    .in0(\input [3]), .in1(\output [3]), .in2(1'b0), .in3(1'b0), .out(_3A), .sel({clear, not_1_out[0]}));
  Multiplexer #(.select(2), .enable("false")) multiplexer_8 (
    .in0(\input [2]), .in1(\output [2]), .in2(1'b0), .in3(1'b0), .out(_2A), .sel({clear, not_1_out[0]}));
  Multiplexer #(.select(2), .enable("false")) multiplexer_9 (
    .in0(\input [1]), .in1(\output [1]), .in2(1'b0), .in3(1'b0), .out(_1A), .sel({clear, not_1_out[0]}));
  Multiplexer #(.select(2), .enable("false")) multiplexer_10 (
    .in0(\input [0]), .in1(\output [0]), .in2(1'b0), .in3(1'b0), .out(_0A), .sel({clear, not_1_out[0]}));

  // Other names for the same wires on the sheet: _0 = \input [0]; _1 = \input [1]; _2 = \input [2]; _3 = \input [3];
  //   _4 = \input [4]; _5 = \input [5]; _6 = \input [6]; _7 = \input [7]; _8 = \input [8]; _9 = \input [9];
  //   S = \output [0]; R = \output [1]; P = \output [2]; O = \output [3]; N = \output [4]; M = \output [5];
  //   L = \output [6]; K = \output [7]; J = \output [8]; I = \output [9]
endmodule

module cmpJump (
  input  enable,
  input  [2:0] Cmp_Jump_Code,
  input  CF,
  input  ZF,
  output out_5
);

  wire and_1_out, and_2_out, and_3_out, and_4_out, not_1_out;

  and and_1 (and_1_out, ZF, ~CF);  // AND_Gate
  and and_2 (and_2_out, ~ZF, ~CF);  // AND_Gate
  and and_3 (and_3_out, ~ZF, CF);  // AND_Gate
  not not_1 (not_1_out, CF);
  and and_4 (and_4_out, ZF, CF);
  Multiplexer #(.select(3)) multiplexer_1 (
    .in0(and_1_out), .in1(and_2_out), .in2(and_3_out), .in3(not_1_out), .in4(and_4_out), .out(out_5),
    .sel(Cmp_Jump_Code), .en(enable));  // open: in5, in6, in7

  // Other names for the same wires on the sheet: CmpJumpCode[2:0] = Cmp_Jump_Code; JumpForCmp = out_5

  // Notes on the sheet:
  //   JE ZF=1 CF=0
  //   JA ZF=0 CF=0
  //   JB ZF=0 CF=1
  //   JAE CF=0
  //   JBE CF=1 ZF=1
  //   000 JE, 001 JA, 010 JB, 011 JAE, 100 JBE
endmodule
